# Fritzing sketch ba_cablage (saved by Fritzing 1.0.1rc)
breadboards: 1

parts:
  J1 = Basic Servo
  LED1 = LED - 5mm [color="Red (633nm)" current=0.030 package="5 mm [THT]"]
  R1 = Resistor [tolerance=±5% power=0.25 resistance=100 package=THT]
  LED2 = LED - 5mm [color="Yellow (595nm)" current=0.030 package="5 mm [THT]"]
  R2 = Resistor [tolerance=±5% power=0.25 resistance=100 package=THT]
  S1 = Toggle Switch [package=THT]
  M1 = IR break beam 3mm rx [package=THT]  # not connected
  M2 = IR break beam 3mm tx [package=THT]  # not connected
  M3 = IR break beam 3mm rx [package=THT]  # not connected
  M4 = IR break beam 3mm tx [package=THT]  # not connected
  Part1 = Arduino Uno (Rev3)

nets:
  GND: J1.gnd, R1.Pin_1, R2.Pin_1, S1.L1, Part1.GND
  VCC: J1.vcc, S1.L2, Part1.5V
  N1: J1.pulse, Part1.D10_PWM/SS
  N2: LED1.cathode, R1.Pin_0
  N3: LED1.anode, Part1.D4
  N4: LED2.cathode, R2.Pin_0
  N5: LED2.anode, Part1.D3_PWM
  N6: S1.COM, Part1.D7

custom parts:
  IR break beam 3mm rx: Infrared break beam Sensor rx module.
  IR break beam 3mm tx: Infrared break beam Sensor tx module.
